# Fritzing sketch hall (saved by Fritzing 0.7.1b)
breadboards: 1

parts:
  IC1 = SO08 [chip_label=IC spacing=300mil package=SO]
  Pad1 = Pad [width=1.5 height=3 connect=south]
  Pad2 = Pad [width=1.5 height=3 connect=south]
  Pad3 = Pad [width=1.5 height=3 connect=south]
  Pad4 = Pad [width=1.5 height=3 connect=south]
  C1 = Ceramic Capacitor [capacitance=100nF package="0603 [SMD, multilayer]"]
  C2 = Ceramic Capacitor [capacitance=100nF package="0603 [SMD, multilayer]"]
  C3 = Ceramic Capacitor [capacitance=100nF package="0603 [SMD, multilayer]"]
  C4 = Ceramic Capacitor [capacitance=100nF package="0603 [SMD, multilayer]"]

nets:
  N1: IC1.1, Pad1.pad, C2.0
  N2: IC1.2, IC1.3, IC1.6, IC1.8, Pad2.pad, C1.0, C2.1, C3.1, C4.0
  N3: IC1.4, Pad4.pad, C4.1
  N4: IC1.5, Pad3.pad, C3.0
  N5: IC1.7, C1.1
